# Fritzing sketch Remote Car and Auto Car (saved by Fritzing 1.0.0d)
breadboards: 1

parts:
  M2 = gear-motor
  M3 = gear-motor
  J1 = Power Jack [package=power_jack_pth_lock]
  A1 = Arduino UNO R4 WiFi
  M5 = RioRand LM2596
  L298N1 = L298N DC motor driver
  Part1 = HY-SRF05 Ultrasonic Rangefinder
  ESP32_-_Back1 = ESP32 - CAM
  Part2 = TXB0108 8-channel Bi-directional Logic Level Converter
  M6 = gear-motor
  M7 = gear-motor
  J2 = Basic Servo
  HC-SR04_Sensor_1 = HC-SR04 Ultrasonic Distance Sensor
  HC-SR04_Sensor_2 = HC-SR04 Ultrasonic Distance Sensor

nets:
  N1: M2.pin_1, L298N1.OUT1, M6.pin_1
  N2: M2.pin_2, L298N1.OUT2, M6.pin_2
  N3: M3.pin_1, L298N1.OUT4, M7.pin_1
  N4: M3.pin_2, L298N1.OUT3, M7.pin_2
  GND: J1.GND, M5.Pin_2, L298N1.GND
  N5: J1.PWR, M5.Pin_1, L298N1.12V
  N6: A1.Pin_34, Part2.B2
  N7: A1.Pin_35, Part2.B1
  N8: A1.Pin_36, HC-SR04_Sensor_1.TRIG
  N9: A1.Pin_37, HC-SR04_Sensor_1.ECHO
  N10: A1.Pin_38, HC-SR04_Sensor_2.TRIG
  N11: A1.Pin_39, HC-SR04_Sensor_2.ECHO
  N12: A1.Pin_40, J2.pulse
  N13: A1.Pin_41, Part1.Echo
  N14: A1.Pin_42, Part1.Trig
  N15: A1.Pin_43, L298N1.ENA, L298N1.ENB
  N16: A1.Pin_44, L298N1.IN4
  N17: A1.Pin_45, L298N1.IN3
  N18: A1.Pin_46, L298N1.IN2
  N19: A1.Pin_47, L298N1.IN1
  VCC: M5.Pin_3, Part1.Vcc, ESP32_-_Back1.5V, Part2.VCCB, J2.vcc, HC-SR04_Sensor_1.VCC, HC-SR04_Sensor_2.VCC
  GND_2: M5.Pin_4, Part1.GND, ESP32_-_Back1.GND, Part2.GND, J2.gnd, HC-SR04_Sensor_1.GND, HC-SR04_Sensor_2.GND
  N20: ESP32_-_Back1.3.3V, Part2.OE, Part2.VCCA
  N21: ESP32_-_Back1.GPIO3_/_RX, Part2.A1
  N22: ESP32_-_Back1.GPIO1_/_TX, Part2.A2

notes:
  12V Battery
  12V -> 5V Buck Converter

custom parts:
  Arduino UNO R4 WiFi: The Arduino UNO R4 WiFi merges the RA4M1 microprocessor from Renesas with the ESP32-S3 from Espressif, creating an all-in-one tool for makers with enhanced processing power and a diverse array of new peripherals.
  L298N DC motor driver: 2x DC motor driver with 78M05 positive voltage regulator (7..35 V) L298N: max 46 V, 2 A Set 5 V Enable jumper to enable 5 V regultor (needed for the L298N) and +5 V output at screw terminal or supply external +5 V at screw terminal Set ENA and/or ENB to +5 V to enable motor permanently or supply ENA and/or ENB with PWM signal IN1 and IN2 set rotation directory for motor A (OUT1/OUT2) IN2 and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
  ESP32 - CAM: The ESP32-CAM has a very competitive small-size camera module that can operate independently as a minimum system with a footprint of only 27*40.5*4.5mm and a deep sleep current of up to 6mA.
  TXB0108 8-channel Bi-directional Logic Level Converter: Because the Arduino (and Basic Stamp) are 5V devices, and most modern sensors, displays, flash cards and modes are 3.3V-only, many makers find that they need to perform level shifting/conversion to protect the 3.3V device from 5V. Although one can use resistors to make a divider, for high speed transfers, the resistors can add a lot of slew and cause havoc that is tough to debug. For that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
